# Fritzing sketch BedLed (saved by Fritzing 0.9.3b)
circuit board: 3.26181cm x 2.99152cm
breadboards: 1

parts:
  Q1 = MOSFET-NCHANNEL [part_number=IRFZ44N package=to220v]
  IC2 = Voltage Regulator [part_number=LM7805 package=to220-igo]
  U1 = attiny85 [package=dip]
  R1 = Resistor [tolerance=±5% resistance=10M package=THT]
  C3 = Ceramic Capacitor [capacitance=10pF package="100 mil [THT, multilayer]"]
  LED = Screw terminal - 2 pins [package=THT]
  Power_plug = Power plug
  Sense = Screw terminal - 2 pins [package=THT]
  C1 = Ceramic Capacitor [capacitance=0.33µF voltage=16V package="100 mil [THT, multilayer]"]
  C2 = Ceramic Capacitor [capacitance=0.1µF package="100 mil [THT, multilayer]"]
  D1 = Schottky Diode 700mil [package="700 mil [THT]"]
  J2 = male pin header, 2 pins [form="♂ (male)"]
  J1 = male pin header, 3 pins [form="♂ (male)"]
  J4 = male pin header, 1 pin [form="♂ (male)"]
  J3 = male pin header, 2 pins [form="♂ (male)"]

nets:
  N1: Q1.G, J1.pin2
  N2: Q1.D, LED.pin2
  GND: Q1.S, IC2.GND, U1.Pin_4, C3.1, Power_plug.GND, Sense.pin1, C1.0, C2.1, J2.pin2, J3.pin2
  12V: IC2.IN, LED.pin1, C1.1, D1.cathode
  5V: IC2.OUT, U1.Pin_8, C2.0, J4.pin1
  N3: U1.Pin_1, J3.pin1
  N4: U1.Pin_2, R1.Pin_1
  N5: U1.Pin_3, R1.Pin_0, C3.0, Sense.pin2
  N6: U1.Pin_5, J1.pin3
  N7: U1.Pin_6, J1.pin1
  N8: U1.Pin_7, J2.pin1
  N9: Power_plug.VCC, D1.anode

notes:
  Power Management
  LED Control
  Cap. Sensing
  9-20V ≤3A
  PWR
  LED
  SENS
  Chris van Marle
  +
  -
  IN
  Sense
  BedLed 2016
  ⏚
  ⍑

custom parts:
  Schottky Diode 700mil: A standard schottky barrier rectifier diode - 700mil
