# Fritzing sketch BedLed_button_schema (saved by Fritzing 0.9.3b)
breadboards: 1

parts:
  S1 = Toggle Switch [package=THT]
  LED1 = LED - 5mm [color="Red (633nm)" package="5 mm [THT]"]
  R1 = TRIMPOT [package=trimpot-5mm]

nets:
  N1: S1.L1, R1.CW
  GND: S1.COM
  Button pin: S1.L2
  N2: LED1.cathode, R1.WIPER
  5V: LED1.anode
